# Fritzing sketch Project (saved by Fritzing 0.9.3b)

parts:
  A1 = GY-BMP280 Breakout
  A2 = DHT22 module
  microSD1 = MicroSD Card Module
  A3 = NEO-6M GPS Module [part_number=GY-GPS6MV2]
  U2 = ESP8266-01S [part_number=ESP8266]
  M1 = DC Motor
  M2 = DC Motor
  M3 = DC Motor
  M4 = DC Motor
  Часть2 = Bluetooth HC-05 Macho
  L298N1 = L298N DC motor driver
  L298N2 = L298N DC motor driver
  S1 = Toggle Switch [package=THT]
  BAT1 = Battery
  Часть3 = Arduino Mega 2560 (Rev3)
  R1 = Resistor [tolerance=±5% resistance=10 package=THT]
  R2 = Resistor [tolerance=±5% resistance=20 package=THT]

nets:
  VCC: A1.Pin_1, A2.+, microSD1.VCC, A3.Vcc, Часть2.VCC, Часть3.5V
  GND: A1.Pin_2, A2.-, microSD1.GND, A3.GND, Часть2.GND, Часть3.GND, R1.Pin_0
  N1: A1.Pin_3, Часть3.D21/SCL
  N2: A1.Pin_4, Часть3.D20/SDA
  N3: A2.Out, Часть3.D31
  N4: microSD1.MISO, Часть3.D23
  N5: microSD1.MOSI, Часть3.D25
  N6: microSD1.SCK, Часть3.D27
  N7: microSD1.CS, Часть3.D29
  N8: A3.Tx, Часть3.D17_PWM/RX2
  N9: A3.Rx, Часть3.D16_PWM/TX2
  N10: U2.RXD, Часть3.D15/RX3
  VCC_2: U2.VCC, U2.CH_PD, Часть2.Key, Часть3.3V3
  N11: U2.TXD, Часть3.D14/TX3
  N12: M1.pin_1, L298N2.OUT4
  N13: M1.pin_2, L298N2.OUT3
  N14: M2.pin_1, L298N2.OUT2
  N15: M2.pin_2, L298N2.OUT1
  N16: M3.pin_1, L298N1.OUT2
  N17: M3.pin_2, L298N1.OUT1
  N18: M4.pin_1, L298N1.OUT4
  N19: M4.pin_2, L298N1.OUT3
  N20: Часть2.State, Часть3.D7_PWM
  N21: Часть2.TXD, Часть3.D0_RX0
  N22: Часть2.RXD, R1.Pin_1, R2.Pin_0
  N23: L298N1.ENA, L298N1.ENB, L298N2.ENA, Часть3.D6_PWM
  N24: L298N1.IN1, Часть3.D2_PWM
  N25: L298N1.IN2, Часть3.D3_PWM
  N26: L298N1.IN3, Часть3.D4_PWM
  N27: L298N1.IN4, Часть3.D5_PWM
  N28: L298N2.GND, BAT1.-
  N29: L298N2.IN1, Часть3.D8_PWM
  N30: L298N2.IN2, Часть3.D9_PWM
  N31: L298N2.IN3, Часть3.D10_PWM
  N32: L298N2.IN4, Часть3.D11_PWM
  N33: S1.COM, BAT1.+
  N34: Часть3.D1_TX0, R2.Pin_1

custom parts:
  DHT22 module: DHT22 module. Pins VCC Data GND.
  MicroSD Card Module: A common microSD card module.
  NEO-6M GPS Module: GY-GPS6MV2 NEO-6M GPS Module Module based on U-blox NEO-6M GPS engine, incorporating regulator for 3.3-5V DC input, MS621FE-compatible rechargeable battery for backup and EEPROM for storing configuration settings. Links: NEO-6 series product information page NEO-6 Datasheet
  L298N DC motor driver: 2x DC motor driver with 78M05 positive voltage regulator (7..35 V) L298N: max 46 V, 2 A Set 5 V Enable jumper to enable 5 V regultor (needed for the L298N) and +5 V output at screw terminal or supply external +5 V at screw terminal Set ENA and/or ENB to +5 V to enable motor permanently or supply ENA and/or ENB with PWM signal IN1 and IN2 set rotation directory for motor A (OUT1/OUT2) IN2 and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
  Battery: Your standard 2x 18650 battery pack (7.4 Volts)
